// Digital circuit SAP.dig as structural Verilog
module SAP (
  input  CLOCK
);

  wire AI, ALU_c_o, and_1_out, AO, AUTO_out, BI, CE, CF, CLK, CLR, CO, EO, FI, HLT, II, IO, J, jk_ff_1_q, MI,
       multiplexer_1_out, nand_1_out, nand_2_out, nCLK, nor_1_out, nor_2_out, not_1_out, not_2_out, OI,
       or_2_out, RESET_out, RI, RO, STEP_out, SU, xor_1_out, ZF;
  wire [2:0] STEP_2_out;
  wire [3:0] A_q, A_q_2, ALU_s, ALU_s_2, driver_1_out, driver_1_out_2, MAR_q, PC_out, register_1_q,
       xor_2_out, xor_2_out_2;
  wire [7:0] B_q, IR_q, multiplexer_2_out, OUT_q;

  Button STEP (.out(STEP_out));
  not not_1 (not_1_out, HLT);
  Button RESET (.out(RESET_out));
  Register #(.Bits(4)) register_1 (.D(driver_1_out), .C(nCLK), .en(J), .Q(register_1_q));
  DipSwitch CLEAR (.out(CLR));
  and and_1 (and_1_out, CLR, STEP_out);
  DipSwitch #(.dipDefault("true")) AUTO (.out(AUTO_out));
  not not_2 (not_2_out, AUTO_out);
  JK_FF jk_ff_1 (.J(not_1_out), .C(CLOCK), .K(not_1_out), .Q(jk_ff_1_q));  // open: nQ
  Seven_Seg_Hex seven_seg_hex_1 (.d(IR_q[7:4]), .dp(1'b0));
  LED led_1 (.in(ZF));
  LED led_2 (.in(CF));
  Multiplexer multiplexer_1 (.sel(and_1_out), .in_0(nCLK), .in_1(1'b0), .out(multiplexer_1_out));
  nand nand_1 (nand_1_out, STEP_out, not_1_out);
  nand nand_2 (nand_2_out, not_2_out, jk_ff_1_q);
  Seven_Seg_Hex seven_seg_hex_2 (.d({1'b0, STEP_2_out}), .dp(1'b0));
  Register #(.Bits(4), .isProgramCounter("true")) MAR (.D(driver_1_out), .C(nCLK), .en(MI), .Q(MAR_q));
  or or_1 (CLK, ~nand_1_out, ~nand_2_out);  // Or
  Register #(.Bits(8), .isProgramCounter("true")) IR (.D({driver_1_out_2, driver_1_out}), .C(nCLK), .en(II), .Q(IR_q));
  CounterPreset #(.Bits(4)) PC (
    .en(CE), .C(multiplexer_1_out), .dir(1'b0), .in(register_1_q), .ld(J), .clr(CLR), .out(PC_out));  // open: ovf
  assign {driver_1_out_2, driver_1_out} = IO ? {4'b0000, IR_q[3:0]} : 8'bz;  // Driver driver_1
  Seven_Seg_Hex seven_seg_hex_3 (.d(driver_1_out_2), .dp(1'b0));
  not not_3 (nCLK, CLK);
  LED W6 (.in(driver_1_out_2[2]));
  LED W7 (.in(driver_1_out_2[3]));
  xor xor_1 (xor_1_out, RESET_out, CLK);
  assign {driver_1_out_2, driver_1_out} = CO ? {4'b0000, PC_out} : 8'bz;  // Driver driver_2
  RAMDualPort #(.AddrBits(4), .Bits(8)) RAM (
    .A(MAR_q), .Din({driver_1_out_2, driver_1_out}), .str(RI), .C(CLK), .ld(RO),
    .D({driver_1_out_2, driver_1_out}));
  Seven_Seg_Hex seven_seg_hex_4 (.d(driver_1_out), .dp(1'b0));
  LED W4 (.in(driver_1_out_2[0]));
  LED W5 (.in(driver_1_out_2[1]));
  or or_2 (or_2_out, CLR, nor_1_out);
  LED W2 (.in(driver_1_out[2]));
  LED W3 (.in(driver_1_out[3]));
  Seven_Seg_Hex seven_seg_hex_5 (.d(PC_out), .dp(1'b0));
  LED W0 (.in(driver_1_out[0]));
  LED W1 (.in(driver_1_out[1]));
  Counter #(.Bits(3)) STEP_2 (.en(1'b1), .C(xor_1_out), .clr(or_2_out), .out(STEP_2_out));  // open: ovf
  ROM #(.AddrBits(9), .Bits(16)) MICROCODE (
    .A({ZF, CF, IR_q[7:4], STEP_2_out}), .sel(1'b1),
    .D({HLT, MI, RI, RO, IO, II, AI, AO, EO, SU, BI, OI, CE, CO, J, FI}));
  Register #(.Bits(8), .isProgramCounter("true")) OUT (
    .D({driver_1_out_2, driver_1_out}), .C(nCLK), .en(OI), .Q(OUT_q));
  Seven_Seg_Hex seven_seg_hex_6 (.d(A_q_2), .dp(1'b0));
  Register #(.Bits(8), .isProgramCounter("true")) A (
    .D({driver_1_out_2, driver_1_out}), .C(nCLK), .en(AI), .Q({A_q_2, A_q}));
  assign {driver_1_out_2, driver_1_out} = AO ? {A_q_2, A_q} : 8'bz;  // Driver driver_3
  Register #(.Bits(8), .isProgramCounter("true")) B (.D({driver_1_out_2, driver_1_out}), .C(nCLK), .en(BI), .Q(B_q));
  LED u_J (.in(J));
  LED u_FI (.in(FI));
  Seven_Seg_Hex seven_seg_hex_7 (.d(A_q), .dp(1'b0));
  Multiplexer #(.Bits(8)) multiplexer_2 (.sel(SU), .in_0({8{1'b0}}), .in_1({8{1'b1}}), .out(multiplexer_2_out));
  assign {driver_1_out_2, driver_1_out} = EO ? {ALU_s_2, ALU_s} : 8'bz;  // Driver driver_4
  LED u_CE (.in(CE));
  LED u_CO (.in(CO));
  Seven_Seg_Hex seven_seg_hex_8 (.d(xor_2_out), .dp(1'b0));
  Seven_Seg_Hex seven_seg_hex_9 (.d(xor_2_out_2), .dp(1'b0));
  assign {xor_2_out_2, xor_2_out} = multiplexer_2_out ^ B_q;  // XOr xor_2, 8 bits wide
  LED _5 (.in(OUT_q[5]));
  LED _6 (.in(OUT_q[6]));
  LED _7 (.in(OUT_q[7]));
  LED u_OI (.in(OI));
  LED u_BI (.in(BI));
  Add #(.Bits(8)) ALU (.a({A_q_2, A_q}), .b({xor_2_out_2, xor_2_out}), .c_i(SU), .s({ALU_s_2, ALU_s}), .c_o(ALU_c_o));
  LED _1 (.in(OUT_q[1]));
  LED _2 (.in(OUT_q[2]));
  LED _3 (.in(OUT_q[3]));
  LED _4 (.in(OUT_q[4]));
  LED u_SU (.in(SU));
  LED u_EO (.in(EO));
  Seven_Seg_Hex seven_seg_hex_10 (.d(ALU_s_2), .dp(1'b0));
  LED _0 (.in(OUT_q[0]));
  LED u_AO (.in(AO));
  LED u_AI (.in(AI));
  Seven_Seg_Hex seven_seg_hex_11 (.d(ALU_s), .dp(1'b0));
  LED u_II (.in(II));
  LED u_IO (.in(IO));
  nor nor_1 (nor_1_out, AO, AI, II, IO, RO, RI, MI, HLT, FI, J, CO, CE, OI, BI, SU, EO);
  LED u_RO (.in(RO));
  LED u_RI (.in(RI));
  nor nor_2 (nor_2_out, ALU_s[0], ALU_s[1], ALU_s[2], ALU_s[3], ALU_s_2[0], ALU_s_2[1], ALU_s_2[2], ALU_s_2[3]);
  LED u_MI (.in(MI));
  LED u_HLT (.in(HLT));
  Register u_CF (.D(ALU_c_o), .C(nCLK), .en(FI), .Q(CF));
  Register u_ZF (.D(nor_2_out), .C(nCLK), .en(FI), .Q(ZF));

  // Notes on the sheet:
  //   CLOCK: Hz: 4
  //   Z
  //   C
  //   STEP
  //   OP
  //   BUS
  //   W BUS BITS
  //   PC
  //   contents of MICROCODE (hex, n*v repeats v):
  //   4004,1408,6*0,4004,1408,4800,1200,4*0,4004,1408,4800,1020,281
  //   ,0,0,0,4004,1408,4800,1020,2c1,0,0,0,4004,1408,4800,2100,4*0,4004
  //   ,1408,a00,5*0,4004,1408,802,5*0,4004,1408,6*0,4004,1408,6*0,4004
  //   ,1408,6*0,4004,1408,6*0,4004,1408,6*0,4004,1408,6*0,4004,1408
  //   ,6*0,4004,1408,110,5*0,4004,1408,8000,5*0,4004,1408,6*0,4004,1408
  //   ,4800,1200,4*0,4004,1408,4800,1020,281,0,0,0,4004,1408,4800,1020
  //   ,2c1,0,0,0,4004,1408,4800,2100,4*0,4004,1408,a00,5*0,4004,1408
  //   ,802,5*0,4004,1408,802,5*0,4004,1408,6*0,4004,1408,6*0,4004,1408
  //   ,6*0,4004,1408,6*0,4004,1408,6*0,4004,1408,6*0,4004,1408,110,5*0
  //   ,4004,1408,8000,5*0,4004,1408,6*0,4004,1408,4800,1200,4*0,4004
  //   ,1408,4800,1020,281,0,0,0,4004,1408,4800,1020,2c1,0,0,0,4004,1408
  //   ,4800,2100,4*0,4004,1408,a00,5*0,4004,1408,802,5*0,4004,1408,6*0
  //   ,4004,1408,802,5*0,4004,1408,6*0,4004,1408,6*0,4004,1408,6*0,4004
  //   ,1408,6*0,4004,1408,6*0,4004,1408,110,5*0,4004,1408,8000,5*0,4004
  //   ,1408,6*0,4004,1408,4800,1200,4*0,4004,1408,4800,1020,281,0,0,0
  //   ,4004,1408,4800,1020,2c1,0,0,0,4004,1408,4800,2100,4*0,4004,1408
  //   ,a00,5*0,4004,1408,802,5*0,4004,1408,802,5*0,4004,1408,802,5*0
  //   ,4004,1408,6*0,4004,1408,6*0,4004,1408,6*0,4004,1408,6*0,4004
  //   ,1408,6*0,4004,1408,110,5*0,4004,1408,8000
  //   A
  //   B
  //   OUTPUT
  //   RESULT
  //   CONTROL SIGNALS
endmodule
